// Logisim project display-controller.circ as structural Verilog: 1 circuit, main circuit display_controller
module display_controller (
  input  [3:0] X_coord,
  input  [3:0] Y_coord,
  input  pixel_state,
  input  write,
  input  pixel_check,
  output [15:0] c00,
  output [15:0] c01,
  output [15:0] c02,
  output [15:0] c03,
  output [15:0] c04,
  output checked,
  output [15:0] c05,
  output [15:0] c06,
  output [15:0] c07,
  output [15:0] c08,
  output [15:0] c09,
  output [15:0] c10,
  output [15:0] c11,
  output [15:0] c12,
  output [15:0] c13,
  output [15:0] c14,
  output [15:0] c15
);

  wire and_17_out, and_18_out, and_19_out, and_20_out, and_21_out, and_22_out, and_23_out, and_24_out,
       and_25_out, and_26_out, and_27_out, and_28_out, and_29_out, and_30_out, and_31_out, and_32_out,
       and_33_out, and_34_out, and_35_out, and_36_out, and_37_out, and_38_out, and_39_out, and_40_out,
       and_41_out, and_42_out, and_43_out, and_44_out, and_45_out, and_46_out, and_47_out, and_48_out,
       or_1_out, or_2_out, or_3_out, or_4_out, wrt0, wrt1, wrt2, wrt3, wrt4, wrt5, wrt6, wrt7, wrt8, wrt9,
       wrt10, wrt11, wrt12, wrt13, wrt14, wrt15;
  wire [15:0] and_1_out, and_2_out, and_3_out, and_4_out, and_5_out, and_6_out, and_7_out, and_8_out,
       and_9_out, and_10_out, and_11_out, and_12_out, and_13_out, and_14_out, and_15_out, and_16_out,
       and_49_out, and_50_out, and_51_out, and_52_out, and_53_out, and_54_out, and_55_out, and_56_out,
       and_57_out, and_58_out, and_59_out, and_60_out, and_61_out, and_62_out, and_63_out, and_64_out,
       checked_value, demultiplexer_3_out0, mask, or_6_out, or_7_out, or_8_out, or_9_out, or_10_out,
       or_11_out, or_12_out, or_13_out, or_14_out, or_15_out, or_16_out, or_17_out, or_18_out, or_19_out,
       or_20_out, or_21_out, value;

  Pull_Resistor pull_resistor_1 (.node(pixel_check));
  or or_1 (or_1_out, pixel_check, write);
  Demultiplexer #(.select(4)) demultiplexer_1 (
    .out0(wrt0), .out1(wrt1), .out2(wrt2), .out3(wrt3), .out4(wrt4), .out5(wrt5), .out6(wrt6), .out7(wrt7),
    .out8(wrt8), .out9(wrt9), .out10(wrt10), .out11(wrt11), .out12(wrt12), .out13(wrt13), .out14(wrt14),
    .out15(wrt15), .in(or_1_out), .sel(X_coord));  // open: en
  Demultiplexer #(.select(4)) demultiplexer_2 (
    .out0(value[0]), .out1(value[1]), .out2(value[2]), .out3(value[3]), .out4(value[4]), .out5(value[5]),
    .out6(value[6]), .out7(value[7]), .out8(value[8]), .out9(value[9]), .out10(value[10]), .out11(value[11]),
    .out12(value[12]), .out13(value[13]), .out14(value[14]), .out15(value[15]), .in(or_2_out), .sel(Y_coord));  // open: en
  or or_2 (or_2_out, pixel_state, pixel_check);
  Demultiplexer #(.select(4)) demultiplexer_3 (
    .out0(demultiplexer_3_out0[0]), .out1(demultiplexer_3_out0[1]), .out2(demultiplexer_3_out0[2]),
    .out3(demultiplexer_3_out0[3]), .out4(demultiplexer_3_out0[4]), .out5(demultiplexer_3_out0[5]),
    .out6(demultiplexer_3_out0[6]), .out7(demultiplexer_3_out0[7]), .out8(demultiplexer_3_out0[8]),
    .out9(demultiplexer_3_out0[9]), .out10(demultiplexer_3_out0[10]), .out11(demultiplexer_3_out0[11]),
    .out12(demultiplexer_3_out0[12]), .out13(demultiplexer_3_out0[13]), .out14(demultiplexer_3_out0[14]),
    .out15(demultiplexer_3_out0[15]), .in(1'b1), .sel(Y_coord));  // open: en
  or or_3 (or_3_out, checked_value[0], checked_value[1], checked_value[2], checked_value[3], checked_value[4], checked_value[5], checked_value[6]);
  or or_4 (or_4_out, checked_value[7], checked_value[8], checked_value[9], checked_value[10], checked_value[11], checked_value[12], checked_value[13]);
  or or_5 (checked, or_3_out, or_4_out, checked_value[14], checked_value[15]);
  // Probe on value
  // Probe on mask
  assign mask = ~demultiplexer_3_out0;  // NOT_Gate not_1, 16 bits wide
  assign and_1_out = c00 & mask;  // AND_Gate and_1, 16 bits wide
  assign and_2_out = c01 & mask;  // AND_Gate and_2, 16 bits wide
  assign and_3_out = c02 & mask;  // AND_Gate and_3, 16 bits wide
  assign and_4_out = c03 & mask;  // AND_Gate and_4, 16 bits wide
  assign and_5_out = c04 & mask;  // AND_Gate and_5, 16 bits wide
  assign and_6_out = c05 & mask;  // AND_Gate and_6, 16 bits wide
  assign and_7_out = c06 & mask;  // AND_Gate and_7, 16 bits wide
  assign and_8_out = c07 & mask;  // AND_Gate and_8, 16 bits wide
  assign and_9_out = c08 & mask;  // AND_Gate and_9, 16 bits wide
  assign and_10_out = c09 & mask;  // AND_Gate and_10, 16 bits wide
  assign and_11_out = c10 & mask;  // AND_Gate and_11, 16 bits wide
  assign and_12_out = c11 & mask;  // AND_Gate and_12, 16 bits wide
  assign and_13_out = c12 & mask;  // AND_Gate and_13, 16 bits wide
  assign and_14_out = c13 & mask;  // AND_Gate and_14, 16 bits wide
  assign and_15_out = c14 & mask;  // AND_Gate and_15, 16 bits wide
  assign and_16_out = c15 & mask;  // AND_Gate and_16, 16 bits wide
  Register #(.width(16)) register_1 (.D(or_6_out), .Q(c00), .clk(and_17_out));  // open: en, clr
  assign or_6_out = value | and_1_out;  // OR_Gate or_6, 16 bits wide
  and and_17 (and_17_out, write, wrt0);
  assign or_7_out = value | and_2_out;  // OR_Gate or_7, 16 bits wide
  Register #(.width(16)) register_2 (.D(or_7_out), .Q(c01), .clk(and_18_out));  // open: en, clr
  and and_18 (and_18_out, write, wrt1);
  Register #(.width(16)) register_3 (.D(or_8_out), .Q(c02), .clk(and_19_out));  // open: en, clr
  assign or_8_out = value | and_3_out;  // OR_Gate or_8, 16 bits wide
  and and_19 (and_19_out, write, wrt2);
  assign or_9_out = value | and_4_out;  // OR_Gate or_9, 16 bits wide
  Register #(.width(16)) register_4 (.D(or_9_out), .Q(c03), .clk(and_20_out));  // open: en, clr
  and and_20 (and_20_out, write, wrt3);
  assign or_10_out = value | and_5_out;  // OR_Gate or_10, 16 bits wide
  Register #(.width(16)) register_5 (.D(or_10_out), .Q(c04), .clk(and_21_out));  // open: en, clr
  and and_21 (and_21_out, write, wrt4);
  Register #(.width(16)) register_6 (.D(or_11_out), .Q(c05), .clk(and_22_out));  // open: en, clr
  assign or_11_out = value | and_6_out;  // OR_Gate or_11, 16 bits wide
  and and_22 (and_22_out, write, wrt5);
  assign or_12_out = value | and_7_out;  // OR_Gate or_12, 16 bits wide
  Register #(.width(16)) register_7 (.D(or_12_out), .Q(c06), .clk(and_23_out));  // open: en, clr
  and and_23 (and_23_out, write, wrt6);
  assign or_13_out = value | and_8_out;  // OR_Gate or_13, 16 bits wide
  Register #(.width(16)) register_8 (.D(or_13_out), .Q(c07), .clk(and_24_out));  // open: en, clr
  and and_24 (and_24_out, write, wrt7);
  assign or_14_out = value | and_9_out;  // OR_Gate or_14, 16 bits wide
  Register #(.width(16)) register_9 (.D(or_14_out), .Q(c08), .clk(and_25_out));  // open: en, clr
  and and_25 (and_25_out, write, wrt8);
  assign or_15_out = value | and_10_out;  // OR_Gate or_15, 16 bits wide
  Register #(.width(16)) register_10 (.D(or_15_out), .Q(c09), .clk(and_26_out));  // open: en, clr
  and and_26 (and_26_out, write, wrt9);
  Register #(.width(16)) register_11 (.D(or_16_out), .Q(c10), .clk(and_27_out));  // open: en, clr
  assign or_16_out = value | and_11_out;  // OR_Gate or_16, 16 bits wide
  and and_27 (and_27_out, write, wrt10);
  assign or_17_out = value | and_12_out;  // OR_Gate or_17, 16 bits wide
  Register #(.width(16)) register_12 (.D(or_17_out), .Q(c11), .clk(and_28_out));  // open: en, clr
  and and_28 (and_28_out, write, wrt11);
  Register #(.width(16)) register_13 (.D(or_18_out), .Q(c12), .clk(and_29_out));  // open: en, clr
  assign or_18_out = value | and_13_out;  // OR_Gate or_18, 16 bits wide
  and and_29 (and_29_out, write, wrt12);
  assign or_19_out = value | and_14_out;  // OR_Gate or_19, 16 bits wide
  Register #(.width(16)) register_14 (.D(or_19_out), .Q(c13), .clk(and_30_out));  // open: en, clr
  and and_30 (and_30_out, write, wrt13);
  assign or_20_out = value | and_15_out;  // OR_Gate or_20, 16 bits wide
  Register #(.width(16)) register_15 (.D(or_20_out), .Q(c14), .clk(and_31_out));  // open: en, clr
  and and_31 (and_31_out, write, wrt14);
  Register #(.width(16)) register_16 (.D(or_21_out), .Q(c15), .clk(and_32_out));  // open: en, clr
  assign or_21_out = value | and_16_out;  // OR_Gate or_21, 16 bits wide
  and and_32 (and_32_out, write, wrt15);
  and and_33 (and_33_out, pixel_check, wrt0);
  and and_34 (and_34_out, pixel_check, wrt1);
  and and_35 (and_35_out, pixel_check, wrt2);
  and and_36 (and_36_out, pixel_check, wrt3);
  and and_37 (and_37_out, pixel_check, wrt4);
  and and_38 (and_38_out, pixel_check, wrt5);
  and and_39 (and_39_out, pixel_check, wrt6);
  and and_40 (and_40_out, pixel_check, wrt7);
  and and_41 (and_41_out, pixel_check, wrt8);
  and and_42 (and_42_out, pixel_check, wrt9);
  and and_43 (and_43_out, pixel_check, wrt10);
  and and_44 (and_44_out, pixel_check, wrt11);
  and and_45 (and_45_out, pixel_check, wrt12);
  and and_46 (and_46_out, pixel_check, wrt13);
  and and_47 (and_47_out, pixel_check, wrt14);
  and and_48 (and_48_out, pixel_check, wrt15);
  assign and_49_out = c00 & value;  // AND_Gate and_49, 16 bits wide
  assign checked_value = and_33_out ? and_49_out : 16'bz;  // Controlled_Buffer controlled_buffer_1
  assign and_50_out = c01 & value;  // AND_Gate and_50, 16 bits wide
  assign checked_value = and_34_out ? and_50_out : 16'bz;  // Controlled_Buffer controlled_buffer_2
  assign checked_value = and_35_out ? and_51_out : 16'bz;  // Controlled_Buffer controlled_buffer_3
  assign and_51_out = c02 & value;  // AND_Gate and_51, 16 bits wide
  assign checked_value = and_36_out ? and_52_out : 16'bz;  // Controlled_Buffer controlled_buffer_4
  assign and_52_out = c03 & value;  // AND_Gate and_52, 16 bits wide
  assign checked_value = and_37_out ? and_53_out : 16'bz;  // Controlled_Buffer controlled_buffer_5
  assign and_53_out = c04 & value;  // AND_Gate and_53, 16 bits wide
  assign and_54_out = c05 & value;  // AND_Gate and_54, 16 bits wide
  assign checked_value = and_38_out ? and_54_out : 16'bz;  // Controlled_Buffer controlled_buffer_6
  assign checked_value = and_39_out ? and_55_out : 16'bz;  // Controlled_Buffer controlled_buffer_7
  assign and_55_out = c06 & value;  // AND_Gate and_55, 16 bits wide
  assign checked_value = and_40_out ? and_56_out : 16'bz;  // Controlled_Buffer controlled_buffer_8
  assign and_56_out = c07 & value;  // AND_Gate and_56, 16 bits wide
  assign and_57_out = c08 & value;  // AND_Gate and_57, 16 bits wide
  assign checked_value = and_41_out ? and_57_out : 16'bz;  // Controlled_Buffer controlled_buffer_9
  assign checked_value = and_42_out ? and_58_out : 16'bz;  // Controlled_Buffer controlled_buffer_10
  assign and_58_out = c09 & value;  // AND_Gate and_58, 16 bits wide
  assign and_59_out = c10 & value;  // AND_Gate and_59, 16 bits wide
  assign checked_value = and_43_out ? and_59_out : 16'bz;  // Controlled_Buffer controlled_buffer_11
  assign and_60_out = c11 & value;  // AND_Gate and_60, 16 bits wide
  assign checked_value = and_44_out ? and_60_out : 16'bz;  // Controlled_Buffer controlled_buffer_12
  assign and_61_out = c12 & value;  // AND_Gate and_61, 16 bits wide
  assign checked_value = and_45_out ? and_61_out : 16'bz;  // Controlled_Buffer controlled_buffer_13
  assign and_62_out = c13 & value;  // AND_Gate and_62, 16 bits wide
  assign checked_value = and_46_out ? and_62_out : 16'bz;  // Controlled_Buffer controlled_buffer_14
  assign and_63_out = c14 & value;  // AND_Gate and_63, 16 bits wide
  assign checked_value = and_47_out ? and_63_out : 16'bz;  // Controlled_Buffer controlled_buffer_15
  assign and_64_out = c15 & value;  // AND_Gate and_64, 16 bits wide
  assign checked_value = and_48_out ? and_64_out : 16'bz;  // Controlled_Buffer controlled_buffer_16
  Pull_Resistor pull_resistor_2 (.node(checked_value));
  // Probe on checked_value
  Pull_Resistor pull_resistor_3 (.node(checked_value));
  // Probe on checked_value
  Pull_Resistor pull_resistor_4 (.node(checked_value));
  // Probe on checked_value
  Pull_Resistor pull_resistor_5 (.node(checked_value));
  // Probe on checked_value
  Pull_Resistor pull_resistor_6 (.node(checked_value));
  // Probe on checked_value
  Pull_Resistor pull_resistor_7 (.node(checked_value));
  // Probe on checked_value
  Pull_Resistor pull_resistor_8 (.node(checked_value));
  // Probe on checked_value
  Pull_Resistor pull_resistor_9 (.node(checked_value));
  // Probe on checked_value
  Pull_Resistor pull_resistor_10 (.node(checked_value));
  // Probe on checked_value
  Pull_Resistor pull_resistor_11 (.node(checked_value));
  // Probe on checked_value
  Pull_Resistor pull_resistor_12 (.node(checked_value));
  // Probe on checked_value
  Pull_Resistor pull_resistor_13 (.node(checked_value));
  // Probe on checked_value
  Pull_Resistor pull_resistor_14 (.node(checked_value));
  // Probe on checked_value
  Pull_Resistor pull_resistor_15 (.node(checked_value));
  // Probe on checked_value
  Pull_Resistor pull_resistor_16 (.node(checked_value));
  // Probe on checked_value
  Pull_Resistor pull_resistor_17 (.node(checked_value));
  // Probe on checked_value

  // Other names for the same wires on the sheet: check = pixel_check
endmodule
